// Logisim project Custom-Library.circ as structural Verilog: 7 circuits, main circuit 4 Bit Mux Module
module _4_Bit_Mux_Module (
  input  A0,
  input  A1,
  input  A2,
  input  A3,
  input  B0,
  input  B1,
  input  B2,
  input  B3,
  input  SELECTION,
  output _0,
  output _1,
  output _2,
  output _3
);

  // _74157 74157_1: pin names not known; wires that end beside it: SELECTION, A0, B0, _0, A1, B1, _1, 1'b0, 1'b1, 1'b0, A3, B3, _3, A2, B2, _2
endmodule

module _2_bit_Mux_Module (
  input  A0,
  input  A1,
  input  B0,
  input  B1,
  input  SELECTION,
  output out_6,
  output out_7
);

  // _74157 74157_1: pin names not known; wires that end beside it: SELECTION, A0, B0, out_6, A1, B1, out_7, 1'b0, 1'b1, 1'b0
endmodule

// MUX
module _10_Bit_Mux_Module (
  input  [9:0] B,
  input  SELECTION,
  input  [9:0] A,
  output [9:0] \output 
);

  _4_Bit_Mux_Module u_4_bit_mux_module_1 (
    .SELECTION(SELECTION), .A0(A[0]), .A1(A[1]), .A2(A[2]), .A3(A[3]), .B0(B[0]), .B1(B[1]), .B2(B[2]),
    .B3(B[3]), ._0(\output [0]), ._1(\output [1]), ._2(\output [2]), ._3(\output [3]));
  _4_Bit_Mux_Module u_4_bit_mux_module_2 (
    .SELECTION(SELECTION), .A0(A[4]), .A1(A[5]), .A2(A[6]), .A3(A[7]), .B0(B[4]), .B1(B[5]), .B2(B[6]),
    .B3(B[7]), ._0(\output [4]), ._1(\output [5]), ._2(\output [6]), ._3(\output [7]));
  _2_bit_Mux_Module u_2_bit_mux_module_1 (
    .SELECTION(SELECTION), .A0(A[8]), .A1(A[9]), .B0(B[8]), .B1(B[9]), .out_6(\output [8]),
    .out_7(\output [9]));

  // Notes on the sheet:
  //   A
endmodule

module Normalizer (
  input  [31:0] Input,
  input  [10:0] Larger_Exponent,
  output [20:0] Final_21_bit_Fraction_Output,
  output [4:0] Shift_Amount,
  output All_0s,
  output [31:0] input_for_rounding,
  output b_out,
  output [9:0] Exponent_After_Normalization,
  output To_detect_negative,
  output Sign_Bit_of_Exponent
);

  wire bitfinder_1_found;
  wire [10:0] subtractor_1_out;
  wire [31:0] shifter_1_out;

  Subtractor #(.width(11)) subtractor_1 (
    .a({{6{1'b0}}, Shift_Amount}), .b(11'h2), .out(subtractor_1_out), .bin(1'b0), .bout(To_detect_negative));
  BitFinder #(.width(32)) bitfinder_1 (
    .in({Input[0], Input[1], Input[2], Input[3], Input[4], Input[5], Input[6], Input[7], Input[8], Input[9], Input[10], Input[11], Input[12], Input[13], Input[14], Input[15], Input[16], Input[17], Input[18], Input[19], Input[20], Input[21], Input[22], Input[23], Input[24], Input[25], Input[26], Input[27], Input[28], Input[29], Input[30], 1'b0}),
    .index(Shift_Amount), .found(bitfinder_1_found));
  Shifter #(.width(32)) shifter_1 (
    .in(Input), .\dist (Shift_Amount),
    .out({shifter_1_out[31], Final_21_bit_Fraction_Output, input_for_rounding[7:0], shifter_1_out[1:0]}));
  // _7404 NOTGate__IC: pin names not known; wires that end beside it: bitfinder_1_found, All_0s
  Subtractor #(.width(11)) subtractor_2 (
    .a(Larger_Exponent), .b(subtractor_1_out), .out({Sign_Bit_of_Exponent, Exponent_After_Normalization}),
    .bin(1'b0), .bout(b_out));

  assign input_for_rounding[31:8] = {3'b001, Final_21_bit_Fraction_Output};

  // Notes on the sheet:
  //   Shift Amount of Normalization
  //   if this subtractor result is positive then exponent will decrease 
  //   if this subtractor result is negative then exponent will increase
  //   Shift amount in 10 bits
  //   Shifter
  //   Significand 1
endmodule

module Overflow_or_Underflow (
  input  [9:0] Exponent_bits_after_normalization,
  input  Fraction_All_0s_or_not,
  input  Sign_Bit_of_Exponent_From_Normalization,
  output Overflow,
  output Underflow
);

  wire bitfinder_1_found, bitfinder_2_found, n7404_1_p2, n7404_1_p4, n7408_1_p3;

  BitFinder #(.width(10), .\type ("low0")) bitfinder_1 (
    .in(Exponent_bits_after_normalization), .found(bitfinder_1_found));  // open: index
  BitFinder #(.width(10)) bitfinder_2 (
    .in(Exponent_bits_after_normalization), .found(bitfinder_2_found));  // open: index
  // _7404 7404_1: pin names not known; wires that end beside it: bitfinder_2_found, n7404_1_p2, Fraction_All_0s_or_not, n7404_1_p4, bitfinder_1_found, Overflow
  // _7408 7408_1: pin names not known; wires that end beside it: n7404_1_p2, n7404_1_p4, n7408_1_p3
  // _7432 7432_1: pin names not known; wires that end beside it: n7408_1_p3, Sign_Bit_of_Exponent_From_Normalization, Underflow
endmodule

module _32_bit_Mux_Module (
  input  [31:0] Input_0,
  input  [31:0] Input_1,
  input  Selection,
  output [31:0] Output
);

  _16_bit_Mux_Module u_16_bit_mux_module_1 (
    .Selection(Selection), .Input_0(Input_0[15:0]), .Output(Output[15:0]), .Input_1(Input_1[15:0]));
  _16_bit_Mux_Module u_16_bit_mux_module_2 (
    .Selection(Selection), .Input_0(Input_0[31:16]), .Output(Output[31:16]), .Input_1(Input_1[31:16]));
endmodule

module _16_bit_Mux_Module (
  input  [15:0] Input_1,
  input  Selection,
  input  [15:0] Input_0,
  output [15:0] Output
);

  _4_Bit_Mux_Module u_4_bit_mux_module_1 (
    .SELECTION(Selection), .A0(Input_0[0]), .A1(Input_0[1]), .A2(Input_0[2]), .A3(Input_0[3]),
    .B0(Input_1[0]), .B1(Input_1[1]), .B2(Input_1[2]), .B3(Input_1[3]), ._0(Output[0]), ._1(Output[1]),
    ._2(Output[2]), ._3(Output[3]));
  _4_Bit_Mux_Module u_4_bit_mux_module_2 (
    .SELECTION(Selection), .A0(Input_0[4]), .A1(Input_0[5]), .A2(Input_0[6]), .A3(Input_0[7]),
    .B0(Input_1[4]), .B1(Input_1[5]), .B2(Input_1[6]), .B3(Input_1[7]), ._0(Output[4]), ._1(Output[5]),
    ._2(Output[6]), ._3(Output[7]));
  _4_Bit_Mux_Module u_4_bit_mux_module_3 (
    .SELECTION(Selection), .A0(Input_0[8]), .A1(Input_0[9]), .A2(Input_0[10]), .A3(Input_0[11]),
    .B0(Input_1[8]), .B1(Input_1[9]), .B2(Input_1[10]), .B3(Input_1[11]), ._0(Output[8]), ._1(Output[9]),
    ._2(Output[10]), ._3(Output[11]));
  _4_Bit_Mux_Module u_4_bit_mux_module_4 (
    .SELECTION(Selection), .A0(Input_0[12]), .A1(Input_0[13]), .A2(Input_0[14]), .A3(Input_0[15]),
    .B0(Input_1[12]), .B1(Input_1[13]), .B2(Input_1[14]), .B3(Input_1[15]), ._0(Output[12]), ._1(Output[13]),
    ._2(Output[14]), ._3(Output[15]));
endmodule
