// Logisim project main.circ as structural Verilog: 9 circuits, main circuit main
// Main Adder
module main (
  input  [31:0] A,
  input  [31:0] B,
  output [31:0] Smaller_Exponent_Significant,
  output [4:0] Difference_in_Exponent,
  output [31:0] Larger_Exponent_Significant,
  output [9:0] Larger_Exponent,
  output [31:0] out_7,
  output Storing_output_Sign_Bit,
  output [31:0] out_9,
  output [20:0] Output_fraction_after_1str_normalization,
  output [9:0] Exponent_after_1st_normalization,
  output OF_after_1st_NRM,
  output UF_after_1st_NRM,
  output [20:0] Output_fraction_after_2nd_normalization,
  output [9:0] Exponent_after_2nd_normalization,
  output OF_after_2nd_NRM,
  output UF_after_2nd_NRM,
  output [31:0] Result,
  output Underflow,
  output Overflow
);

  wire Exponent_Comparator_x__y, Exponent_Comparator_x_y, n7404_1__2__1y, n7432_1__3__1y, n74157_1__4__y1,
       normalizer_1_all_0s, normalizer_1_sign_bit_of_exponent, normalizer_2_all_0s,
       normalizer_2_sign_bit_of_exponent;
  wire [31:0] n32_bit_mux_module_1_output, normalizer_1_input_for_rounding, rounding_1_output, shifter_1_out,
       sign_adjustment_1_output_32_bit_significand__after_sign_adjustment,
       sign_adjustment_2_output_32_bit_significand__after_sign_adjustment;

  Comparator Exponent_Comparator (
    .X(A[30:21]), .Y(B[30:21]), .X__Y(Exponent_Comparator_x__y), .X_Y(Exponent_Comparator_x_y),
    .Difference(Difference_in_Exponent), .Larger(Larger_Exponent));  // open: out_5
  Sign_Adjustment sign_adjustment_1 (
    .Input_32_bit_significand({3'b001, A[20:0], {8{1'b0}}}), .Sign_Bit(A[31]),
    .Output_32_bit_significand__after_sign_adjustment(sign_adjustment_1_output_32_bit_significand__after_sign_adjustment));
  _32_bit_Mux_Module _32_bit_MUX (
    .Input_0(sign_adjustment_1_output_32_bit_significand__after_sign_adjustment),
    .Input_1(sign_adjustment_2_output_32_bit_significand__after_sign_adjustment),
    .Selection(Exponent_Comparator_x__y), .Output(Smaller_Exponent_Significant));
  _32_bit_Mux_Module u_32_bit_mux_module_1 (
    .Input_0({Storing_output_Sign_Bit, Exponent_after_2nd_normalization, Output_fraction_after_2nd_normalization}),
    .Input_1({Storing_output_Sign_Bit, Exponent_after_1st_normalization, Output_fraction_after_1str_normalization}),
    .Selection(n7432_1__3__1y), .Output(n32_bit_mux_module_1_output));
  Shifter #(.width(32), .shift("ar")) shifter_1 (
    .in(Smaller_Exponent_Significant), .\dist (Difference_in_Exponent), .out(shifter_1_out));
  _32_bit_Mux_Module u_32_bit_mux_module_2 (
    .Input_0(n32_bit_mux_module_1_output), .Input_1({32{1'b0}}), .Selection(normalizer_1_all_0s),
    .Output(Result));
  Adder #(.width(32)) adder_1 (
    .a(shifter_1_out), .b(Larger_Exponent_Significant), .out(out_7), .cin(1'b0));  // open: cout
  _32_bit_Mux_Module _32_Bit_MUX_2 (
    .Input_0(sign_adjustment_1_output_32_bit_significand__after_sign_adjustment),
    .Input_1(sign_adjustment_2_output_32_bit_significand__after_sign_adjustment),
    .Selection(Exponent_Comparator_x_y), .Output(Larger_Exponent_Significant));
  Complementing_result complementing_result_1 (
    .Input(out_7), .Output(out_9), .Result_Sign_Bit(Storing_output_Sign_Bit));
  _7404 u_7404_1 (
    ._1__1A(normalizer_1_all_0s), ._2__1Y(n7404_1__2__1y));  // open: _3__2A, _4__2Y, _5__3A, _6__3Y, _7__GND, _14__Vcc, _13__6A, _12__6Y, _11__5A, _10__5Y, _9__4A, _8__4Y
  Overflow_or_Underflow overflow_or_underflow_1 (
    .Exponent_bits_after_normalization(Exponent_after_1st_normalization),
    .Fraction_All_0s_or_not(normalizer_1_all_0s),
    .Sign_Bit_of_Exponent_From_Normalization(normalizer_1_sign_bit_of_exponent), .Overflow(OF_after_1st_NRM),
    .Underflow(UF_after_1st_NRM));
  Normalizer normalizer_1 (
    .Input(out_9), .Larger_Exponent({1'b0, Larger_Exponent}),
    .Final_21_bit_Fraction_Output(Output_fraction_after_1str_normalization), .All_0s(normalizer_1_all_0s),
    .input_for_rounding(normalizer_1_input_for_rounding),
    .Exponent_After_Normalization(Exponent_after_1st_normalization),
    .Sign_Bit_of_Exponent(normalizer_1_sign_bit_of_exponent));  // open: Shift_Amount, b_out, To_detect_negative
  _7432 u_7432_1 (
    ._1__1A(OF_after_1st_NRM), ._2__1B(UF_after_1st_NRM), ._3__1Y(n7432_1__3__1y));  // open: _4__2A, _5__2B, _6__2Y, _7__GND, _14__Vcc, _13__4B, _12__4A, _11__4Y, _10__3B, _9__3A, _8__3Y
  _7408 u_7408_1 (
    ._1__1A(n74157_1__4__y1), ._2__1B(n7404_1__2__1y), ._3__1Y(Underflow));  // open: _4__2A, _5__2B, _6__2Y, _7__GND, _14__Vcc, _13__4B, _12__4A, _11__4Y, _10__3B, _9__3A, _8__3Y
  Sign_Adjustment sign_adjustment_2 (
    .Input_32_bit_significand({3'b001, B[20:0], {8{1'b0}}}), .Sign_Bit(B[31]),
    .Output_32_bit_significand__after_sign_adjustment(sign_adjustment_2_output_32_bit_significand__after_sign_adjustment));
  Rounding rounding_1 (.\input (normalizer_1_input_for_rounding), .\output (rounding_1_output));
  _74157 u_74157_1 (
    ._1__S(n7432_1__3__1y), ._2__A1(UF_after_2nd_NRM), ._3__B1(UF_after_1st_NRM), ._4__Y1(n74157_1__4__y1),
    ._5__A2(OF_after_2nd_NRM), ._6__B2(OF_after_1st_NRM), ._7__Y2(Overflow), ._15__G(1'b0));  // open: _8__GND, _16__Vcc, _14__A4, _13__B4, _12__Y4, _11__A3, _10__B3, _9__Y3
  Normalizer normalizer_2 (
    .Input(rounding_1_output), .Larger_Exponent({1'b0, Exponent_after_1st_normalization}),
    .Final_21_bit_Fraction_Output(Output_fraction_after_2nd_normalization), .All_0s(normalizer_2_all_0s),
    .Exponent_After_Normalization(Exponent_after_2nd_normalization),
    .Sign_Bit_of_Exponent(normalizer_2_sign_bit_of_exponent));  // open: Shift_Amount, input_for_rounding, b_out, To_detect_negative
  Overflow_or_Underflow overflow_or_underflow_2 (
    .Exponent_bits_after_normalization(Exponent_after_2nd_normalization),
    .Fraction_All_0s_or_not(normalizer_2_all_0s),
    .Sign_Bit_of_Exponent_From_Normalization(normalizer_2_sign_bit_of_exponent), .Overflow(OF_after_2nd_NRM),
    .Underflow(UF_after_2nd_NRM));

  // Notes on the sheet:
  //   ABSOLUTE ZERO
  //   If "All 0's" =1 ,then no matter what ABSOLUTE ZERO will be selected for output 
  //   Output after 1st normalization (if overflow or underflow occurs)
  //   this 32 bit MUX is for selecting result after 1st NRM or 2nd NRM
  //   MUX for finding smaller significand
  //   Adjusting sign
  //   Arethmetic right shift 
  //   this 32 bit MUX is for handling special case of All zeros
  //   MUX for finding larger significand
  //   significand adder
  //   For 1st Overflow and underflow
  //   Output after 2nd normalization
  //   Complementing result
  //   Result of significand addition
  //   1st Normalizer
  //   Adjusting sign
  //   Rounder
  //   2nd Normalizer
  //   For 2nd Overflow and underflow
  //   MUX for selecting correct OF and UF
endmodule

module Comparator (
  input  [9:0] X,
  input  [9:0] Y,
  output X__Y,
  output X_Y,
  output out_5,
  output [4:0] Difference,
  output [9:0] Larger
);

  wire comparator_1_eq, comparator_1_gt, comparator_2_gt;
  wire [4:0] subtractor_1_out_2;
  wire [9:0] _10_bit_MUX_2_output;
  wire [9:5] subtractor_1_out;

  Comparator_part #(.width(10), .mode("unsigned")) comparator_1 (
    .a(X), .b(Y), .gt(comparator_1_gt), .eq(comparator_1_eq), .lt(X_Y));
  _7432 u_7432_1 (
    ._1__1A(comparator_1_gt), ._2__1B(comparator_1_eq), ._3__1Y(X__Y));  // open: _4__2A, _5__2B, _6__2Y, _7__GND, _14__Vcc, _13__4B, _12__4A, _11__4Y, _10__3B, _9__3A, _8__3Y
  _10_Bit_Mux_Module _10_Bit_MUX (.SELECTION(X_Y), .A(X), .B(Y), .\output (Larger));
  _10_Bit_Mux_Module _10_bit_MUX_2 (.SELECTION(X__Y), .A(X), .B(Y), .\output (_10_bit_MUX_2_output));
  Subtractor #(.width(10)) subtractor_1 (
    .a(Larger), .b(_10_bit_MUX_2_output), .out({subtractor_1_out, subtractor_1_out_2}), .bin(1'b0),
    .bout(out_5));
  Comparator_part #(.width(10), .mode("unsigned")) comparator_2 (
    .a(10'h1f), .b({subtractor_1_out, subtractor_1_out_2}), .gt(comparator_2_gt));  // open: eq, lt
  _5_bit_Mux_Module u_5_bit_mux_module_1 (
    .Input_0({5{1'b1}}), .Selection(comparator_2_gt), .Output(Difference), .Input_1(subtractor_1_out_2));

  // Notes on the sheet:
  //   Exponent of A
  //   Exponent of B
  //   10 Bit comparator
  //   Selecting Larger
  //   Selecting Smaller
  //   10 Bit subtractor
  //   0000011111
  //   31 > diff hoile diff jacche, r naile 31 hacche
endmodule

module Sign_Adjustment (
  input  [31:0] Input_32_bit_significand,
  input  Sign_Bit,
  output [31:0] Output_32_bit_significand__after_sign_adjustment
);

  wire [31:0] negator_1_out;

  Negator #(.width(32)) negator_1 (.in(Input_32_bit_significand), .out(negator_1_out));
  _32_bit_Mux_Module u_32_bit_mux_module_1 (
    .Input_0(Input_32_bit_significand), .Input_1(negator_1_out), .Selection(Sign_Bit),
    .Output(Output_32_bit_significand__after_sign_adjustment));

  // Notes on the sheet:
  //   2's complementer
endmodule

module Complementing_result (
  input  [31:0] Input,
  output [31:0] Output,
  output Result_Sign_Bit
);

  wire [31:0] negator_1_out;

  Negator #(.width(32)) negator_1 (.in(Input), .out(negator_1_out));
  _32_bit_Mux_Module u_32_bit_mux_module_1 (
    .Input_0(Input), .Input_1(negator_1_out), .Selection(Input[31]), .Output(Output));

  assign Result_Sign_Bit = Input[31];

  // Notes on the sheet:
  //   A and B er significand addition er por result jodi negative hoy tahole "Result Sign Bit" 1 hobe and result er significand 2's complement hoye output hobe
  //   A and B er significand addition er por result jodi positive hoy tahole "Result Sign Bit" 0 hobe and result er significand unchanged obosthay output a jabe
endmodule

module _4_Bit_Mux_Module (
  input  A0,
  input  A1,
  input  A2,
  input  A3,
  input  B0,
  input  B1,
  input  B2,
  input  B3,
  input  SELECTION,
  output _0,
  output _1,
  output _2,
  output _3
);

  _74157 u_74157_1 (
    ._1__S(SELECTION), ._2__A1(A0), ._3__B1(B0), ._4__Y1(_0), ._5__A2(A1), ._6__B2(B1), ._7__Y2(_1),
    ._8__GND(1'b0), ._16__Vcc(1'b1), ._15__G(1'b0), ._14__A4(A3), ._13__B4(B3), ._12__Y4(_3), ._11__A3(A2),
    ._10__B3(B2), ._9__Y3(_2));
endmodule

module _2_bit_Mux_Module (
  input  A0,
  input  A1,
  input  B0,
  input  B1,
  input  SELECTION,
  output out_6,
  output out_7
);

  _74157 u_74157_1 (
    ._1__S(SELECTION), ._2__A1(A0), ._3__B1(B0), ._4__Y1(out_6), ._5__A2(A1), ._6__B2(B1), ._7__Y2(out_7),
    ._8__GND(1'b0), ._16__Vcc(1'b1), ._15__G(1'b0));  // open: _14__A4, _13__B4, _12__Y4, _11__A3, _10__B3, _9__Y3
endmodule

// MUX
module _10_Bit_Mux_Module (
  input  [9:0] B,
  input  SELECTION,
  input  [9:0] A,
  output [9:0] \output 
);

  _4_Bit_Mux_Module u_4_bit_mux_module_1 (
    .SELECTION(SELECTION), .A0(A[0]), .A1(A[1]), .A2(A[2]), .A3(A[3]), .B0(B[0]), .B1(B[1]), .B2(B[2]),
    .B3(B[3]), ._0(\output [0]), ._1(\output [1]), ._2(\output [2]), ._3(\output [3]));
  _4_Bit_Mux_Module u_4_bit_mux_module_2 (
    .SELECTION(SELECTION), .A0(A[4]), .A1(A[5]), .A2(A[6]), .A3(A[7]), .B0(B[4]), .B1(B[5]), .B2(B[6]),
    .B3(B[7]), ._0(\output [4]), ._1(\output [5]), ._2(\output [6]), ._3(\output [7]));
  _2_bit_Mux_Module u_2_bit_mux_module_1 (
    .SELECTION(SELECTION), .A0(A[8]), .A1(A[9]), .B0(B[8]), .B1(B[9]), .out_6(\output [8]),
    .out_7(\output [9]));

  // Notes on the sheet:
  //   A
endmodule

module Floating_Point_Adder (
  input  [31:0] A,
  input  [31:0] B,
  output OVERFLOW,
  output UNDERFLOW,
  output [31:0] RESULT
);

  main main_1 (
    .A(A), .B(B), .Result(RESULT), .Underflow(UNDERFLOW), .Overflow(OVERFLOW));  // open: Larger_Exponent, Smaller_Exponent_Significant, Difference_in_Exponent, Larger_Exponent_Significant, out_7, Storing_output_Sign_Bit, out_9, Output_fraction_after_1str_normalization, Exponent_after_1st_normalization, OF_after_1st_NRM, UF_after_1st_NRM, Output_fraction_after_2nd_normalization, Exponent_after_2nd_normalization, OF_after_2nd_NRM, UF_after_2nd_NRM
endmodule

module _5_bit_Mux_Module (
  input  [4:0] Input_0,
  input  [4:0] Input_1,
  input  Selection,
  output [4:0] Output
);

  _4_Bit_Mux_Module u_4_bit_mux_module_1 (
    .SELECTION(Selection), .A0(Input_0[0]), .A1(Input_0[1]), .A2(Input_0[2]), .A3(Input_0[3]),
    .B0(Input_1[0]), .B1(Input_1[1]), .B2(Input_1[2]), .B3(Input_1[3]), ._0(Output[0]), ._1(Output[1]),
    ._2(Output[2]), ._3(Output[3]));
  _74157 u_74157_1 (
    ._1__S(Selection), ._2__A1(Input_0[4]), ._3__B1(Input_1[4]), ._4__Y1(Output[4]), ._15__G(1'b0));  // open: _5__A2, _6__B2, _7__Y2, _8__GND, _16__Vcc, _14__A4, _13__B4, _12__Y4, _11__A3, _10__B3, _9__Y3
endmodule
