// Logisim project ALU.circ as structural Verilog: 8 circuits, main circuit main
module main (
  input  [3:0] Input_1,
  input  [3:0] Input_2,
  input  [2:0] ALUOp,
  output Overflow,
  output Zero,
  output [3:0] Output
);

  wire add_1_overflow, sub_1_overflow;
  wire [3:0] add_1_result, and_1_result, nor_1_result, or_1_result, sll_1_result, srl_1_result, sub_1_result;

  add add_1 (.X(Input_1), .Y(Input_2), .Result(add_1_result), .Overflow(add_1_overflow));
  sub sub_1 (.X(Input_1), .Y(Input_2), .Zero(Zero), .Result(sub_1_result), .Overflow(sub_1_overflow));
  \and  and_1 (.X(Input_1), .Y(Input_2), .Result(and_1_result));
  \or  or_1 (.X(Input_1), .Y(Input_2), .Result(or_1_result));
  \nor  nor_1 (.X(Input_1), .Y(Input_2), .Result(nor_1_result));
  sll sll_1 (.X(Input_1), .Y(Input_2), .Result(sll_1_result));
  srl srl_1 (.X(Input_1), .Y(Input_2), .Result(srl_1_result));
  Multiplexer #(.select(3), .enable("false")) multiplexer_1 (
    .in0(add_1_overflow), .in1(sub_1_overflow), .in2(1'b0), .in3(1'b0), .in4(1'b0), .in5(1'b0), .in6(1'b0),
    .in7(1'b0), .out(Overflow), .sel(ALUOp));
  Multiplexer #(.select(3), .width(4), .enable("false")) multiplexer_2 (
    .in0(add_1_result), .in1(sub_1_result), .in2(and_1_result), .in3(or_1_result), .in4(nor_1_result),
    .in5(sll_1_result), .in6(srl_1_result), .out(Output), .sel(ALUOp));  // open: in7
endmodule

module add (
  input  [3:0] X,
  input  [3:0] Y,
  output [3:0] Result,
  output Overflow
);

  wire adder_1_cout, adder_2_cout;

  Adder #(.width(3)) adder_1 (.a(X[2:0]), .b(Y[2:0]), .out(Result[2:0]), .cout(adder_1_cout));  // open: cin
  Adder #(.width(1)) adder_2 (.a(X[3]), .b(Y[3]), .out(Result[3]), .cin(adder_1_cout), .cout(adder_2_cout));
  xor xor_1 (Overflow, adder_1_cout, adder_2_cout);
endmodule

module sub (
  input  [3:0] X,
  input  [3:0] Y,
  output Zero,
  output [3:0] Result,
  output Overflow
);

  wire or_1_out;
  wire [3:0] negator_1_out;

  Negator #(.width(4)) negator_1 (.in(Y), .out(negator_1_out));
  add add_1 (.X(X), .Y(negator_1_out), .Result(Result), .Overflow(Overflow));
  not not_1 (Zero, or_1_out);
  or or_1 (or_1_out, Result[0], Result[1], Result[2], Result[3]);
endmodule

module \and  (
  input  [3:0] X,
  input  [3:0] Y,
  output [3:0] Result
);

  assign Result = X & Y;  // AND_Gate and_1, 4 bits wide
endmodule

module \or  (
  input  [3:0] X,
  input  [3:0] Y,
  output [3:0] Result
);

  assign Result = X | Y;  // OR_Gate or_1, 4 bits wide
endmodule

module \nor  (
  input  [3:0] X,
  input  [3:0] Y,
  output [3:0] Result
);

  assign Result = ~(X | Y);  // NOR_Gate nor_1, 4 bits wide
endmodule

module sll (
  input  [3:0] X,
  input  [3:0] Y,
  output [3:0] Result
);

  Shifter #(.width(4)) shifter_1 (.in(X), .\dist (Y[1:0]), .out(Result));
endmodule

module srl (
  input  [3:0] X,
  input  [3:0] Y,
  output [3:0] Result
);

  Shifter #(.width(4), .shift("ar")) shifter_1 (.in(X), .\dist (Y[1:0]), .out(Result));
endmodule
