// Logisim project Control_Unit.circ as structural Verilog: 1 circuit, main circuit Control Unit
module Control_Unit (
  input  [3:0] Op_Code,
  output RegDst,
  output Jump,
  output Beq,
  output Bneq,
  output MemRead,
  output MemToReg,
  output [2:0] ALUOp,
  output MemWrite,
  output ALUSrc,
  output RegWrite
);

  ROM #(.addrWidth(4), .dataWidth(12)) rom_1 (
    .addr(Op_Code), .data({RegWrite, ALUSrc, MemWrite, ALUOp, MemToReg, MemRead, Bneq, Beq, Jump, RegDst}));  // open: sel
  // Probe on {RegWrite, ALUSrc, MemWrite, ALUOp, MemToReg, MemRead, Bneq, Beq, Jump, RegDst}

  // Notes on the sheet:
  //   contents of rom_1 (hex, n*v repeats v):
  //   801 d80 cc0 d40 901 2 c30 44 841 c40 881 c80 8c1 600 c00 48
endmodule
